// Digital circuit sap-4.dig as structural Verilog
module sap_4 (
  input  [2:0] Opcode,
  input  Enable_Registers,
  input  [63:0] Argument,
  input  Clock,
  output [63:0] Program_counter_value,
  output [63:0] Argument_Value,
  output [63:0] Accumulator_value
);

  wire and_1_out, and_2_out, and_3_out, and_4_out, and_5_out, and_6_out, and_7_out, decoder_1_out_1,
       decoder_1_out_2, decoder_1_out_3, decoder_1_out_4, decoder_1_out_5, decoder_1_out_6, not_3_out,
       not_4_out, not_5_out, not_6_out, not_7_out, not_8_out, or_1_out;
  wire [63:0] multiplexer_1_out, multiplexer_2_out, nor_1_out, not_1_out, not_2_out, RAM_d;

  assign not_1_out = ~Argument_Value;  // Not not_1, 64 bits wide
  Register #(.Bits(64)) Accumulator (.D(nor_1_out), .C(and_6_out), .en(Enable_Registers), .Q(Accumulator_value));
  assign not_2_out = ~not_1_out;  // Not not_2, 64 bits wide
  CounterPreset #(.Bits(64), .isProgramCounter("true")) Program_Counter (
    .en(Enable_Registers), .C(not_3_out), .dir(1'b0), .in(not_2_out), .ld(and_1_out), .clr(1'b0),
    .out(Program_counter_value));  // open: ovf
  Register #(.Bits(64)) u_Argument (.D(multiplexer_1_out), .C(not_6_out), .en(Enable_Registers), .Q(Argument_Value));
  assign nor_1_out = ~(Accumulator_value | Argument_Value);  // NOr nor_1, 64 bits wide
  and and_1 (and_1_out, and_4_out, Accumulator_value[63]);
  not not_3 (not_3_out, not_4_out);
  Multiplexer #(.Bits(64)) multiplexer_1 (
    .sel(and_2_out), .in_0(multiplexer_2_out), .in_1(RAM_d), .out(multiplexer_1_out));
  not not_4 (not_4_out, Clock);
  not not_5 (not_5_out, or_1_out);
  not not_6 (not_6_out, not_5_out);
  and and_2 (and_2_out, Clock, decoder_1_out_6);
  or or_1 (or_1_out, and_7_out, and_2_out, and_3_out);
  Multiplexer #(.Bits(64)) multiplexer_2 (
    .sel(and_7_out), .in_0(Program_counter_value), .in_1(Argument), .out(multiplexer_2_out));
  and and_3 (and_3_out, Clock, decoder_1_out_5);
  RAMDualPort #(.AddrBits(24), .Bits(64)) RAM (
    .A(Argument_Value[23:0]), .Din(Accumulator_value), .str(and_5_out), .C(not_8_out), .ld(1'b1), .D(RAM_d));
  and and_4 (and_4_out, Clock, decoder_1_out_4);
  and and_5 (and_5_out, Clock, decoder_1_out_3);
  Decoder #(.Selector_Bits(3)) decoder_1 (
    .sel(Opcode), .out_1(decoder_1_out_1), .out_2(decoder_1_out_2), .out_3(decoder_1_out_3),
    .out_4(decoder_1_out_4), .out_5(decoder_1_out_5), .out_6(decoder_1_out_6));  // open: out_0, out_7
  and and_6 (and_6_out, Clock, decoder_1_out_2);
  not not_7 (not_7_out, Clock);
  not not_8 (not_8_out, not_7_out);
  and and_7 (and_7_out, Clock, decoder_1_out_1);

  // Notes on the sheet:
  //   Opcode: The opcode that will be executed.
endmodule
